// Logisim project var3.circ as structural Verilog: 1 circuit, main circuit main
module main (
  input  clk,
  input  rst_n,
  input  shift_in,
  input  t,
  output q
);

  wire d_ff_1_q, multiplexer_1_out, not_1_out, xor_1_out;
  wire [7:0] and_1_out;
  wire [7:7] register_1_q;

  not not_1 (not_1_out, rst_n);
  xor xor_1 (xor_1_out, q, t);
  Multiplexer multiplexer_1 (.in0(1'b0), .in1(xor_1_out), .out(multiplexer_1_out), .sel(rst_n));  // open: en
  D_Flip_Flop d_ff_1 (.clk(clk), .D(not_1_out), .Q(d_ff_1_q), .reset(rst_n));  // open: Qn, preset, en
  and and_1 (and_1_out[0], shift_in, rst_n);
  D_Flip_Flop d_ff_2 (.clk(clk), .D(multiplexer_1_out), .Q(q));  // open: Qn, preset, en, reset
  Register register_1 (.D(and_1_out), .Q({register_1_q[7], and_1_out[7:1]}), .clk(clk), .clr(d_ff_1_q));  // open: en
endmodule
