// Logisim project task2.circ as structural Verilog: 1 circuit, main circuit main
module main (
  input  clk,
  input  rst_n,
  input  [3:0] data,
  input  sel,
  output y
);

  wire d_ff_1_qn, shift_register_1_q0;

  D_Flip_Flop d_ff_1 (.clk(clk), .D(rst_n), .Qn(d_ff_1_qn), .preset(rst_n));  // open: Q, en, reset
  Shift_Register shift_register_1 (
    .in(data[0]), .clk(clk), .clr(d_ff_1_qn), .q0(shift_register_1_q0));  // open: shift, out, load, d0, d1, q1, d2, q2, d3, q3, d4, q4, d5, q5, d6, q6, d7, q7
  Multiplexer multiplexer_1 (.in0(1'b0), .in1(shift_register_1_q0), .out(y), .sel(sel));  // open: en
endmodule
