// Logisim project Task2.circ as structural Verilog: 1 circuit, main circuit main
module main (
  input  clk,
  input  rst_n,
  input  d,
  input  t,
  output q_ff,
  output q_tff
);

  wire and_1_out, d_ff_1_qn, d_ff_3_qn;

  D_Flip_Flop d_ff_1 (.clk(clk), .D(rst_n), .Qn(d_ff_1_qn), .preset(rst_n));  // open: Q, en, reset
  and and_1 (and_1_out, t, d_ff_3_qn);
  D_Flip_Flop d_ff_2 (.clk(clk), .D(d), .Q(q_ff), .reset(d_ff_1_qn));  // open: Qn, preset, en
  D_Flip_Flop d_ff_3 (.clk(clk), .D(and_1_out), .Q(q_tff), .Qn(d_ff_3_qn), .reset(d_ff_1_qn));  // open: preset, en
endmodule
