// Logisim project Вариант 3.circ as structural Verilog: 1 circuit, main circuit main
module main (
  input  [2:0] a,
  input  b,
  output OUT
);

  wire decoder_1_out5, decoder_1_out7, xor_1_out;
  wire [2:0] decoder_1_out1;

  Decoder #(.select(3), .enable("false")) decoder_1 (
    .out1(decoder_1_out1[0]), .out2(decoder_1_out1[1]), .out4(decoder_1_out1[2]), .out5(decoder_1_out5),
    .out7(decoder_1_out7), .sel(a));  // open: out0, out3, out6
  xor xor_1 (xor_1_out, decoder_1_out5, decoder_1_out7);
  Multiplexer #(.select(3), .disabled(0)) multiplexer_1 (
    .in0(xor_1_out), .in1(1'b1), .in2(1'b0), .in3(1'b0), .in4(1'b1), .in5(1'b1), .in6(1'b0), .in7(1'b0),
    .out(OUT), .sel(decoder_1_out1), .en(b));
endmodule
