// Logisim project Task2.circ as structural Verilog: 1 circuit, main circuit main
module main (
  input  clk,
  input  j,
  input  k,
  input  t,
  input  rst_n,
  output q_jk,
  output q_tff
);

  wire and_1_out, and_2_out, and_3_out, d_ff_1_qn, d_ff_2_qn, not_1_out, not_2_out, or_1_out;

  not not_1 (not_1_out, j);
  and and_1 (and_1_out, j, not_2_out, 1'b1);
  and and_2 (and_2_out, 1'b0, k, not_1_out);
  and and_3 (and_3_out, d_ff_2_qn, j, k);
  not not_2 (not_2_out, k);
  D_Flip_Flop d_ff_1 (.clk(clk), .D(rst_n), .Qn(d_ff_1_qn), .preset(rst_n));  // open: Q, en, reset
  or or_1 (or_1_out, and_1_out, and_2_out, and_3_out);
  D_Flip_Flop d_ff_2 (.clk(clk), .D(or_1_out), .Q(q_jk), .Qn(d_ff_2_qn), .reset(d_ff_1_qn));  // open: preset, en
  T_Flip_Flop t_ff_1 (.clk(clk), .T(t), .Q(q_tff), .reset(d_ff_1_qn));  // open: Qn, preset, en
endmodule
