// Logisim project Task52.circ as structural Verilog: 1 circuit, main circuit main
module main (
  input  shift_in,
  input  clk,
  input  rst_n,
  input  [3:0] data,
  output [7:0] shift_reg,
  output [1:0] out_6
);

  wire d_ff_1_qn;

  Shift_Register shift_register_1 (
    .in(shift_in), .clk(clk), .clr(d_ff_1_qn), .q0(shift_reg[0]), .q1(shift_reg[1]), .q2(shift_reg[2]),
    .q3(shift_reg[3]), .q4(shift_reg[4]), .q5(shift_reg[5]), .q6(shift_reg[6]), .q7(shift_reg[7]));  // open: shift, out, load, d0, d1, d2, d3, d4, d5, d6, d7
  D_Flip_Flop d_ff_1 (.clk(clk), .D(rst_n), .Qn(d_ff_1_qn), .preset(rst_n));  // open: Q, en, reset
  Multiplexer #(.select(4), .width(2), .disabled(0), .enable("false")) multiplexer_1 (
    .in0(2'b00), .in1(2'b00), .in2(2'b01), .in3(2'b00), .in4(2'b10), .in5(2'b00), .in6(2'b00), .in7(2'b00),
    .in8(2'b11), .in9(2'b00), .in10(2'b00), .in11(2'b00), .in12(2'b00), .in13(2'b00), .in14(2'b00),
    .in15(2'b00), .out(out_6), .sel(data));
endmodule
