// Logisim project Вариант 5.circ as structural Verilog: 1 circuit, main circuit main
module main (
  input  [11:0] a,
  input  [11:0] b,
  input  \С ,
  input  [2:0] c,
  output [11:0] f
);

  wire [11:0] nor_1_out, or_1_out, register_1_q;

  assign or_1_out = a | b;  // OR_Gate or_1, 12 bits wide
  assign nor_1_out = ~(a | b);  // NOR_Gate nor_1, 12 bits wide
  Register #(.width(12)) register_1 (.D(or_1_out), .Q(register_1_q), .clk(\С ));  // open: en, clr
  Multiplexer #(.select(3), .width(12), .disabled(0), .enable("false")) multiplexer_1 (
    .in2(a), .in3(register_1_q), .in4(nor_1_out), .in7({12{1'b1}}), .out(f), .sel(c));  // open: in0, in1, in5, in6

  // Notes on the sheet:
  //   f: pull=down
endmodule
