// Logisim project Task62.circ as structural Verilog: 1 circuit, main circuit main
module main (
  input  clk,
  input  shift_in,
  input  rst_n,
  input  d,
  output [7:0] shift_reg,
  output q
);

  wire d_ff_1_qn;

  D_Flip_Flop d_ff_1 (.clk(clk), .D(rst_n), .Qn(d_ff_1_qn), .preset(rst_n));  // open: Q, en, reset
  Shift_Register shift_register_1 (
    .in(shift_in), .clk(clk), .clr(d_ff_1_qn), .q0(shift_reg[0]), .q1(shift_reg[1]), .q2(shift_reg[2]),
    .q3(shift_reg[3]), .q4(shift_reg[4]), .q5(shift_reg[5]), .q6(shift_reg[6]), .q7(shift_reg[7]));  // open: shift, out, load, d0, d1, d2, d3, d4, d5, d6, d7
  D_Flip_Flop d_ff_2 (.clk(clk), .D(d), .Q(q), .reset(d_ff_1_qn));  // open: Qn, preset, en
endmodule
