// Logisim project Вариант 6.circ as structural Verilog: 1 circuit, main circuit main
module main (
  input  [4:0] IN,
  input  [2:0] Sel,
  input  C,
  output [4:0] OUT
);

  wire [4:0] and_1_out, multiplexer_1_out, or_1_out;

  assign or_1_out = OUT | IN;  // OR_Gate or_1, 5 bits wide
  assign and_1_out = OUT & IN;  // AND_Gate and_1, 5 bits wide
  Multiplexer #(.select(3), .width(5), .disabled(0), .enable("false")) multiplexer_1 (
    .in0(OUT), .in1(5'b10001), .in2(or_1_out), .in3({5{1'b0}}), .in4(and_1_out), .in5({5{1'b0}}),
    .in6({5{1'b0}}), .in7({5{1'b0}}), .out(multiplexer_1_out), .sel(Sel));
  Register #(.width(5)) register_1 (.D(multiplexer_1_out), .Q(OUT), .clk(C));  // open: en, clr
endmodule
