// Logisim project Task72.circ as structural Verilog: 1 circuit, main circuit main
module main (
  input  clk,
  input  rst_n,
  input  d,
  output q,
  output [3:0] dec_out
);

  wire multiplexer_1_out;

  Multiplexer multiplexer_1 (.in0(1'b0), .in1(d), .out(multiplexer_1_out), .sel(rst_n));  // open: en
  D_Flip_Flop d_ff_1 (.clk(clk), .D(multiplexer_1_out), .Q(q));  // open: Qn, preset, en, reset
  Decoder decoder_1 (.out0(dec_out[0]), .out1(dec_out[1]), .sel(q));  // open: en

  assign dec_out[3:2] = 2'b00;
endmodule
