// Logisim project Task82.circ as structural Verilog: 1 circuit, main circuit main
module main (
  input  [3:0] data,
  input  [1:0] addr,
  output y,
  output [1:0] enc_out
);

  Multiplexer #(.select(2)) multiplexer_1 (
    .in0(data[0]), .in1(data[1]), .in2(data[2]), .in3(data[3]), .out(y), .sel(addr));  // open: en
  Multiplexer #(.select(4), .width(2), .disabled(0)) multiplexer_2 (
    .in0(2'b00), .in1(2'b00), .in2(2'b01), .in3(2'b00), .in4(2'b10), .in5(2'b00), .in6(2'b00), .in7(2'b00),
    .in8(2'b11), .in9(2'b00), .in10(2'b00), .in11(2'b00), .in12(2'b00), .in13(2'b00), .in14(2'b00),
    .in15(2'b00), .out(enc_out), .sel(data));  // open: en
endmodule
