// Logisim project Вариант 8.circ as structural Verilog: 1 circuit, main circuit main
module main (
  input  [7:0] A,
  input  D,
  input  C,
  output [7:0] out
);

  wire decoder_1_out0, decoder_1_out1;
  wire [7:0] multiplexer_1_out;
  wire [7:2] d_ff_1_q;

  D_Flip_Flop d_ff_1 (.clk(C), .D(D), .Q(d_ff_1_q[2]), .Qn(d_ff_1_q[4]));  // open: preset, en, reset
  Decoder #(.disabled(0), .enable("false")) decoder_1 (.out0(decoder_1_out0), .out1(decoder_1_out1), .sel(out[0]));
  or or_1 (d_ff_1_q[7], decoder_1_out0, decoder_1_out1);
  Multiplexer #(.width(8), .enable("false")) multiplexer_1 (
    .in0(A), .in1({d_ff_1_q[7], 2'b11, d_ff_1_q[4], 1'b1, d_ff_1_q[2], 2'b11}), .out(multiplexer_1_out),
    .sel(out[1]));
  Register register_1 (.D(multiplexer_1_out), .Q(out), .clk(C));  // open: en, clr
endmodule
