// Logisim project Вариант 9.circ as structural Verilog: 1 circuit, main circuit main
module main (
  input  [3:0] A,
  output [3:0] OUT
);

  wire a_t, decoder_1_out0, decoder_1_out1, decoder_1_out2, decoder_1_out3, decoder_1_out4, decoder_1_out5,
       decoder_1_out6, decoder_1_out7, decoder_1_out8, decoder_1_out9, decoder_1_out10, decoder_1_out11,
       decoder_1_out12, decoder_1_out13, decoder_1_out14;

  Decoder #(.select(4)) decoder_1 (
    .out0(decoder_1_out0), .out1(decoder_1_out1), .out2(decoder_1_out2), .out3(decoder_1_out3),
    .out4(decoder_1_out4), .out5(decoder_1_out5), .out6(decoder_1_out6), .out7(decoder_1_out7),
    .out8(decoder_1_out8), .out9(decoder_1_out9), .out10(decoder_1_out10), .out11(decoder_1_out11),
    .out12(decoder_1_out12), .out13(decoder_1_out13), .out14(decoder_1_out14), .out15(a_t), .sel(A), .en(1'b1));
  Priority_Encoder #(.select(4)) priority_encoder_1 (
    .in0(decoder_1_out1), .in1(decoder_1_out2), .in2(decoder_1_out4), .in3(decoder_1_out9),
    .in4(decoder_1_out5), .in5(decoder_1_out3), .in6(decoder_1_out7), .in7(decoder_1_out8),
    .in8(decoder_1_out11), .in9(decoder_1_out0), .in10(decoder_1_out10), .in11(decoder_1_out13),
    .in12(decoder_1_out14), .in13(decoder_1_out6), .in14(decoder_1_out12), .in15(decoder_1_out14), .out(OUT));  // open: gs, en_out, en_in
endmodule
