// Logisim project Task102.circ as structural Verilog: 1 circuit, main circuit main
module main (
  input  j,
  input  clk,
  input  k,
  input  rst_n,
  output q,
  output [1:0] enc_out
);

  wire d_ff_1_qn;

  J_K_Flip_Flop j_k_ff_1 (.J(j), .clk(clk), .K(k), .Q(q), .reset(d_ff_1_qn));  // open: Qn, preset, en
  D_Flip_Flop d_ff_1 (.clk(clk), .D(rst_n), .Qn(d_ff_1_qn), .preset(rst_n));  // open: Q, en, reset
  Multiplexer #(.width(2)) multiplexer_1 (.in0(2'b00), .in1(2'b11), .out(enc_out), .sel(q));  // open: en
endmodule
