// Logisim project Вариант 10.circ as structural Verilog: 1 circuit, main circuit main
module main (
  input  A,
  input  S,
  input  Clk,
  input  R,
  input  J,
  input  K,
  input  D,
  output OUT
);

  wire d_ff_1_q, j_k_ff_1_q, multiplexer_1_out, multiplexer_2_out, multiplexer_3_out, s_r_ff_1_q;

  S_R_Flip_Flop s_r_ff_1 (.S(S), .clk(Clk), .R(R), .Q(s_r_ff_1_q));  // open: Qn, preset, reset, en
  J_K_Flip_Flop j_k_ff_1 (.J(J), .clk(Clk), .K(K), .Q(j_k_ff_1_q));  // open: Qn, preset, en, reset
  D_Flip_Flop d_ff_1 (.clk(Clk), .D(D), .Q(d_ff_1_q));  // open: Qn, preset, en, reset
  Multiplexer #(.enable("false")) multiplexer_1 (.in0(s_r_ff_1_q), .in1(j_k_ff_1_q), .out(multiplexer_1_out), .sel(A));
  Multiplexer #(.enable("false")) multiplexer_2 (.in0(d_ff_1_q), .in1(j_k_ff_1_q), .out(multiplexer_2_out), .sel(A));
  Multiplexer #(.enable("false")) multiplexer_3 (.in0(d_ff_1_q), .in1(s_r_ff_1_q), .out(multiplexer_3_out), .sel(A));
  or or_1 (OUT, multiplexer_1_out, multiplexer_2_out, multiplexer_3_out);
endmodule
