// Logisim project Вариант 11.circ as structural Verilog: 1 circuit, main circuit main
module main (
  input  IN0,
  input  IN1,
  input  C,
  input  IN3,
  input  IN4,
  input  EN,
  output Q,
  output nQ
);

  wire multiplexer_1_out, multiplexer_2_out, multiplexer_3_out, multiplexer_4_out;

  Multiplexer #(.select(2)) multiplexer_1 (
    .in0(IN0), .in1(1'b1), .in2(IN1), .in3(IN3), .out(multiplexer_1_out), .sel({IN4, IN3}), .en(EN));
  Multiplexer multiplexer_2 (.in0(IN0), .in1(1'b1), .out(multiplexer_2_out), .sel(IN4), .en(EN));
  Multiplexer multiplexer_3 (.in0(1'b1), .in1(IN0), .out(multiplexer_3_out), .sel(multiplexer_1_out), .en(EN));
  Multiplexer multiplexer_4 (
    .in0(multiplexer_2_out), .in1(multiplexer_3_out), .out(multiplexer_4_out), .sel(IN3), .en(EN));
  D_Flip_Flop d_ff_1 (.clk(C), .D(multiplexer_4_out), .Q(Q), .Qn(nQ));  // open: preset, en, reset
endmodule
