// Logisim project Вариант 12.circ as structural Verilog: 1 circuit, main circuit main
module main (
  input  \Сlk ,
  input  B,
  input  D,
  input  C,
  input  A,
  input  E,
  output OUT
);

  wire d_ff_1_qn, demultiplexer_1_out0, demultiplexer_1_out1, multiplexer_1_out, shift_register_1_out;

  D_Flip_Flop d_ff_1 (.clk(\Сlk ), .D(B), .Qn(d_ff_1_qn));  // open: Q, preset, en, reset
  Demultiplexer demultiplexer_1 (.out0(demultiplexer_1_out0), .out1(demultiplexer_1_out1), .in(A), .sel(D), .en(1'b1));
  Shift_Register shift_register_1 (
    .in(d_ff_1_qn), .clk(\Сlk ), .out(shift_register_1_out));  // open: shift, load, clr, d0, q0, d1, q1, d2, q2, d3, q3, d4, q4, d5, q5, d6, q6, d7, q7
  Multiplexer multiplexer_1 (.in0(demultiplexer_1_out0), .in1(C), .out(multiplexer_1_out), .sel(E), .en(A));
  or or_1 (OUT, shift_register_1_out, demultiplexer_1_out1, multiplexer_1_out);
endmodule
