// Logisim project Вариант 13.circ as structural Verilog: 1 circuit, main circuit main
module main (
  input  I3,
  input  I0,
  input  I2,
  input  C,
  input  I1,
  output [7:0] OUT1,
  output [7:0] OUT2,
  output OUT
);

  wire decoder_1_out1, or_1_out;
  wire [3:0] shift_register_1_q3, shift_register_2_q0;

  or or_1 (or_1_out, I3, I0);
  Shift_Register #(.length(4)) shift_register_1 (
    .shift(1'b1), .in(or_1_out), .clk(C), .q0(shift_register_1_q3[3]), .q1(shift_register_1_q3[2]),
    .q2(shift_register_1_q3[1]), .q3(shift_register_1_q3[0]));  // open: out, load, clr, d0, d1, d2, d3
  Shift_Register #(.length(4)) shift_register_2 (
    .shift(I2), .in(I1), .clk(C), .load(1'b0), .d0(shift_register_1_q3[3]), .q0(shift_register_2_q0[3]),
    .d1(shift_register_1_q3[2]), .q1(shift_register_2_q0[2]), .d2(shift_register_1_q3[1]),
    .q2(shift_register_2_q0[1]), .d3(shift_register_1_q3[0]), .q3(shift_register_2_q0[0]));  // open: out, clr
  Demultiplexer #(.width(8), .disabled(0), .enable("false")) demultiplexer_1 (
    .out0(OUT1), .out1(OUT2), .in({shift_register_2_q0[2:0], 1'b1, shift_register_1_q3}), .sel(decoder_1_out1));
  Decoder #(.enable("false")) decoder_1 (.out0(OUT), .out1(decoder_1_out1), .sel(shift_register_2_q0[3]));
endmodule
