// Logisim project Вариант14.circ as structural Verilog: 1 circuit, main circuit main
module main (
  input  I1,
  input  I1_2,
  input  I2,
  input  I2_2,
  input  C,
  input  C_2
);

  wire [7:0] multiplexer_1_out, multiplexer_2_out, multiplexer_3_out, multiplexer_4_out, register_1_q,
       register_2_q, register_3_q_2, register_4_q, register_5_q;
  wire [7:4] and_1_out, and_3_out, register_3_q;
  wire [7:7] and_2_out;

  Multiplexer #(.width(8), .enable("false")) multiplexer_1 (
    .in0({and_3_out[7], register_4_q[5:4], and_3_out[4], register_4_q[2], {2{and_3_out[4]}}, register_4_q[7]}),
    .in1(register_2_q), .out(multiplexer_1_out), .sel(I2));
  Register #(.trigger("falling")) register_1 (.D(multiplexer_2_out), .Q(register_1_q), .clk(C));  // open: en, clr
  Multiplexer #(.width(8), .enable("false")) multiplexer_2 (
    .in0(8'h4f),
    .in1({and_3_out[7], register_4_q[5:4], and_3_out[4], register_4_q[2], {2{and_3_out[4]}}, register_4_q[7]}),
    .out(multiplexer_2_out), .sel(I1));
  Register #(.trigger("falling")) register_2 (
    .D(multiplexer_1_out), .Q({register_2_q[6:0], register_2_q[7]}), .clk(C));  // open: en, clr
  Register #(.trigger("falling")) register_3 (
    .D({and_3_out[7], register_4_q[5:4], and_3_out[4], register_4_q[2], {2{and_3_out[4]}}, register_4_q[7]}),
    .Q({register_3_q[7], register_3_q_2[6:5], register_3_q[4], register_3_q_2[3:0]}), .clk(C));  // open: en, clr
  and and_1 (and_1_out[4], register_1_q[0], register_1_q[1], register_1_q[3]);
  not not_1 (and_1_out[7], register_1_q[6]);
  and and_2 (and_2_out[7], register_3_q_2[6], register_3_q[7]);
  Multiplexer #(.width(8), .enable("false")) multiplexer_3 (
    .in0({and_1_out[7], register_1_q[5:4], and_1_out[4], register_1_q[2], {2{and_1_out[4]}}, register_1_q[7]}),
    .in1({and_2_out[7], {2{register_3_q_2[5]}}, register_3_q_2[3], register_3_q_2[1], register_3_q_2[2], register_3_q_2[0], register_3_q_2[6]}),
    .out(multiplexer_3_out), .sel(I2_2));
  Register #(.trigger("falling")) register_4 (.D(multiplexer_4_out), .Q(register_4_q), .clk(C_2));  // open: en, clr
  Multiplexer #(.width(8), .enable("false")) multiplexer_4 (
    .in0({register_5_q[0], register_5_q[7:1]}),
    .in1({and_1_out[7], register_1_q[5:4], and_1_out[4], register_1_q[2], {2{and_1_out[4]}}, register_1_q[7]}),
    .out(multiplexer_4_out), .sel(I1_2));
  Register #(.trigger("falling")) register_5 (.D(multiplexer_3_out), .Q(register_5_q), .clk(C_2));  // open: en, clr
  Register #(.trigger("falling")) register_6 (
    .D({and_1_out[7], register_1_q[5:4], and_1_out[4], register_1_q[2], {2{and_1_out[4]}}, register_1_q[7]}),
    .Q(register_3_q_2), .clk(C_2));  // open: en, clr
  and and_3 (and_3_out[4], register_4_q[0], register_4_q[1], register_4_q[3]);
  not not_2 (and_3_out[7], register_4_q[6]);
  and and_4 (and_2_out[7], register_3_q_2[6], register_3_q_2[7]);
endmodule
