// Logisim project Вариант 15.circ as structural Verilog: 1 circuit, main circuit main
module main (
  input  S,
  input  \Сlk ,
  input  R,
  input  D,
  input  C,
  input  A,
  output OUT
);

  wire demultiplexer_1_out0, multiplexer_1_out, s_r_ff_1_qn, shift_register_1_out;

  S_R_Flip_Flop s_r_ff_1 (.S(S), .clk(\Сlk ), .R(R), .Qn(s_r_ff_1_qn));  // open: Q, preset, reset, en
  Demultiplexer demultiplexer_1 (.out0(demultiplexer_1_out0), .in(A), .sel(D), .en(1'b1));  // open: out1
  Shift_Register shift_register_1 (
    .in(s_r_ff_1_qn), .clk(\Сlk ), .out(shift_register_1_out));  // open: shift, load, clr, d0, q0, d1, q1, d2, q2, d3, q3, d4, q4, d5, q5, d6, q6, d7, q7
  Multiplexer multiplexer_1 (.in0(demultiplexer_1_out0), .in1(C), .out(multiplexer_1_out), .sel(A), .en(1'b1));
  or or_1 (OUT, shift_register_1_out, multiplexer_1_out);
endmodule
