// Logisim project Вариант 16.circ as structural Verilog: 1 circuit, main circuit main
module main (
  input  A,
  input  S,
  input  Clk,
  input  R,
  input  J,
  input  K,
  input  D,
  output OUT1,
  output OUT2,
  output OUT3
);

  wire d_ff_1_q, j_k_ff_1_q, multiplexer_1_out, multiplexer_3_out, s_r_ff_1_q;

  S_R_Flip_Flop s_r_ff_1 (.S(S), .clk(Clk), .R(R), .Q(s_r_ff_1_q));  // open: Qn, preset, reset, en
  J_K_Flip_Flop j_k_ff_1 (.J(J), .clk(Clk), .K(K), .Q(j_k_ff_1_q));  // open: Qn, preset, en, reset
  D_Flip_Flop d_ff_1 (.clk(Clk), .D(D), .Q(d_ff_1_q));  // open: Qn, preset, en, reset
  Multiplexer #(.enable("false")) multiplexer_1 (.in0(s_r_ff_1_q), .in1(j_k_ff_1_q), .out(multiplexer_1_out), .sel(A));
  Multiplexer #(.enable("false")) multiplexer_2 (.in0(d_ff_1_q), .in1(j_k_ff_1_q), .sel(A));  // open: out
  Multiplexer #(.enable("false")) multiplexer_3 (.in0(d_ff_1_q), .in1(s_r_ff_1_q), .out(multiplexer_3_out), .sel(A));
  Shift_Register shift_register_1 (
    .in(multiplexer_3_out), .clk(Clk), .out(OUT1));  // open: shift, load, clr, d0, q0, d1, q1, d2, q2, d3, q3, d4, q4, d5, q5, d6, q6, d7, q7
  Shift_Register shift_register_2 (
    .in(multiplexer_1_out), .clk(Clk), .out(OUT2));  // open: shift, load, clr, d0, q0, d1, q1, d2, q2, d3, q3, d4, q4, d5, q5, d6, q6, d7, q7
  Shift_Register shift_register_3 (
    .in(multiplexer_3_out), .clk(Clk), .out(OUT3));  // open: shift, load, clr, d0, q0, d1, q1, d2, q2, d3, q3, d4, q4, d5, q5, d6, q6, d7, q7
endmodule
