// Logisim project Вариант 17.circ as structural Verilog: 1 circuit, main circuit main
module main (
  input  CLK,
  output [2:0] A
);

  wire decoder_1_out0, decoder_1_out1, decoder_1_out2, decoder_1_out3, decoder_1_out4, decoder_1_out5,
       decoder_1_out6, decoder_1_out7;
  wire [2:0] priority_encoder_1_out;

  Decoder #(.select(3)) decoder_1 (
    .out0(decoder_1_out0), .out1(decoder_1_out1), .out2(decoder_1_out2), .out3(decoder_1_out3),
    .out4(decoder_1_out4), .out5(decoder_1_out5), .out6(decoder_1_out6), .out7(decoder_1_out7), .sel(A),
    .en(1'b1));
  T_Flip_Flop t_ff_1 (.clk(CLK), .T(priority_encoder_1_out[0]), .Q(A[2]));  // open: Qn, preset, reset, en
  Priority_Encoder priority_encoder_1 (
    .in0(decoder_1_out2), .in1(decoder_1_out1), .in2(decoder_1_out3), .in3(decoder_1_out5),
    .in4(decoder_1_out4), .in5(decoder_1_out7), .in6(decoder_1_out0), .in7(decoder_1_out6),
    .out(priority_encoder_1_out));  // open: en_in, gs, en_out
  T_Flip_Flop t_ff_2 (.clk(CLK), .T(priority_encoder_1_out[1]), .Q(A[1]));  // open: Qn, preset, reset, en
  T_Flip_Flop t_ff_3 (.clk(CLK), .T(priority_encoder_1_out[2]), .Q(A[0]));  // open: Qn, preset, reset, en
endmodule
