// Logisim project Вариант 19.circ as structural Verilog: 1 circuit, main circuit main
module main (
  input  CLK,
  input  A,
  output [9:0] OUT
);

  wire and_1_out, t_ff_1_qn, t_ff_2_qn, t_ff_3_qn, t_ff_4_qn, t_ff_5_qn, t_ff_6_qn, t_ff_7_qn, t_ff_8_qn,
       t_ff_9_qn;

  T_Flip_Flop t_ff_1 (.clk(CLK), .T(A), .Q(OUT[0]), .Qn(t_ff_1_qn), .reset(and_1_out));  // open: preset, en
  T_Flip_Flop t_ff_2 (.clk(t_ff_1_qn), .T(A), .Q(OUT[1]), .Qn(t_ff_2_qn), .reset(and_1_out));  // open: preset, en
  T_Flip_Flop t_ff_3 (.clk(t_ff_2_qn), .T(A), .Q(OUT[2]), .Qn(t_ff_3_qn), .reset(and_1_out));  // open: preset, en
  T_Flip_Flop t_ff_4 (.clk(t_ff_3_qn), .T(A), .Q(OUT[3]), .Qn(t_ff_4_qn), .reset(and_1_out));  // open: preset, en
  T_Flip_Flop t_ff_5 (.clk(t_ff_4_qn), .T(A), .Q(OUT[4]), .Qn(t_ff_5_qn), .reset(and_1_out));  // open: preset, en
  T_Flip_Flop t_ff_6 (.clk(t_ff_5_qn), .T(A), .Q(OUT[5]), .Qn(t_ff_6_qn), .reset(and_1_out));  // open: preset, en
  T_Flip_Flop t_ff_7 (.clk(t_ff_6_qn), .T(A), .Qn(t_ff_7_qn), .reset(and_1_out));  // open: Q, preset, en
  T_Flip_Flop t_ff_8 (.clk(t_ff_9_qn), .T(A), .Q(OUT[8]), .Qn(t_ff_8_qn), .reset(and_1_out));  // open: preset, en
  T_Flip_Flop t_ff_9 (.clk(t_ff_7_qn), .T(A), .Q(OUT[7]), .Qn(t_ff_9_qn), .reset(and_1_out));  // open: preset, en
  T_Flip_Flop t_ff_10 (.clk(t_ff_8_qn), .T(A), .Q(OUT[9]), .reset(and_1_out));  // open: Qn, preset, en
  and and_1 (and_1_out, OUT[9], OUT[8]);
endmodule
