// Logisim project Вариант21.circ as structural Verilog: 1 circuit, main circuit main
module main (
  input  [5:0] a,
  input  \С ,
  input  [1:0] a_2,
  output OUT
);

  wire decoder_1_out0, decoder_1_out1, decoder_1_out2, decoder_1_out3, j_k_ff_1_qn, s_r_ff_1_q, t_ff_1_q,
       t_ff_2_qn;

  Decoder #(.select(2), .enable("false")) decoder_1 (
    .out0(decoder_1_out0), .out1(decoder_1_out1), .out2(decoder_1_out2), .out3(decoder_1_out3), .sel(a_2));
  S_R_Flip_Flop #(.trigger("falling")) s_r_ff_1 (
    .S(a[0]), .clk(\С ), .R(a[5]), .Q(s_r_ff_1_q), .en(decoder_1_out0));  // open: Qn, preset, reset
  J_K_Flip_Flop #(.trigger("falling")) j_k_ff_1 (
    .J(a[1]), .clk(\С ), .K(a[2]), .Qn(j_k_ff_1_qn), .en(decoder_1_out1));  // open: Q, preset, reset
  T_Flip_Flop t_ff_1 (.clk(\С ), .T(a[3]), .Q(t_ff_1_q), .en(decoder_1_out2));  // open: Qn, preset, reset
  T_Flip_Flop #(.trigger("falling")) t_ff_2 (
    .clk(\С ), .T(a[4]), .Qn(t_ff_2_qn), .en(decoder_1_out3));  // open: Q, preset, reset
  or or_1 (OUT, s_r_ff_1_q, j_k_ff_1_qn, t_ff_1_q, t_ff_2_qn);
endmodule
