// Logisim project Вариант 22.circ as structural Verilog: 1 circuit, main circuit main
module main (
  input  [4:0] IN,
  input  [2:0] Sel,
  input  EN,
  input  C,
  output [4:0] OUT
);

  wire [4:0] multiplexer_1_out, nor_1_out, or_1_out;

  assign nor_1_out = ~(OUT | IN);  // NOR_Gate nor_1, 5 bits wide
  assign or_1_out = OUT | IN;  // OR_Gate or_1, 5 bits wide
  Multiplexer #(.select(3), .width(5), .disabled(0)) multiplexer_1 (
    .in0(OUT), .in1(5'b00001), .in2(nor_1_out), .in3(5'b10001), .in4(or_1_out), .in5(5'b10001),
    .in6(5'b10001), .in7(5'b10001), .out(multiplexer_1_out), .sel(Sel), .en(EN));
  Register #(.width(5)) register_1 (.D(multiplexer_1_out), .Q(OUT), .clk(C));  // open: en, clr
endmodule
