// Logisim project Вариант 23.circ as structural Verilog: 1 circuit, main circuit main
module main (
  input  [7:0] a,
  input  Q,
  input  a_2,
  input  C,
  output O1,
  output [7:0] O2
);

  Shift_Register shift_register_1 (
    .shift(Q), .in(a_2), .clk(C), .out(O1), .d0(a[7]), .q0(O2[7]), .d1(a[6]), .q1(O2[6]), .d2(a[5]),
    .q2(O2[5]), .d3(a[4]), .q3(O2[4]), .d4(a[3]), .q4(O2[3]), .d5(a[2]), .q5(O2[2]), .d6(a[1]), .q6(O2[1]),
    .d7(a[0]), .q7(O2[0]));  // open: load, clr
endmodule
