// Logisim project Вариант 24.circ as structural Verilog: 1 circuit, main circuit main
module main (
  input  I1,
  input  I2,
  input  C
);

  wire [7:0] multiplexer_1_out, multiplexer_2_out, register_1_q, register_2_q, register_3_q;
  wire [7:7] register_3_q_2;

  Multiplexer #(.width(8), .enable("false")) multiplexer_1 (
    .in0(register_2_q), .in1({register_3_q[7:6], register_3_q[6], register_3_q[4:0]}),
    .out(multiplexer_1_out), .sel(I2));
  Multiplexer #(.width(8), .enable("false")) multiplexer_2 (
    .in0({register_1_q[6:0], register_1_q[7]}), .in1(register_2_q), .out(multiplexer_2_out), .sel(I1));
  Register register_1 (.D(multiplexer_2_out), .Q(register_1_q), .clk(C));  // open: en, clr
  Register register_2 (.D(multiplexer_1_out), .Q({register_2_q[6:0], register_2_q[7]}), .clk(C));  // open: en, clr
  Register register_3 (
    .D(register_2_q),
    .Q({register_3_q_2[7], register_3_q[0], {2{register_3_q[6]}}, register_3_q[4], register_3_q[2], register_3_q[3], register_3_q[1]}),
    .clk(C));  // open: en, clr
  nand nand_1 (register_3_q[7], register_3_q[0], register_3_q_2[7]);
endmodule
