// Logisim project Вариант 25.circ as structural Verilog: 1 circuit, main circuit main
module main (
  input  [3:0] A,
  output [2:0] OUT,
  output O
);

  wire and_1_out, decoder_1_out0, decoder_1_out1, decoder_1_out2, decoder_1_out3, decoder_1_out4,
       decoder_1_out5, decoder_1_out6, decoder_1_out7, decoder_1_out8, decoder_1_out9, decoder_1_out10,
       decoder_1_out11, decoder_1_out12, decoder_1_out13, decoder_1_out14, decoder_1_out15, or_1_out,
       or_2_out;

  Decoder #(.select(4)) decoder_1 (
    .out0(decoder_1_out0), .out1(decoder_1_out1), .out2(decoder_1_out2), .out3(decoder_1_out3),
    .out4(decoder_1_out4), .out5(decoder_1_out5), .out6(decoder_1_out6), .out7(decoder_1_out7),
    .out8(decoder_1_out8), .out9(decoder_1_out9), .out10(decoder_1_out10), .out11(decoder_1_out11),
    .out12(decoder_1_out12), .out13(decoder_1_out13), .out14(decoder_1_out14), .out15(decoder_1_out15),
    .sel(A), .en(1'b1));
  or or_1 (or_1_out, decoder_1_out6, decoder_1_out7, decoder_1_out8, decoder_1_out9, decoder_1_out10);
  or or_2 (or_2_out, decoder_1_out0, decoder_1_out1, decoder_1_out2, decoder_1_out3, decoder_1_out4);
  and and_1 (and_1_out, decoder_1_out11, decoder_1_out12);
  Priority_Encoder priority_encoder_1 (
    .in0(decoder_1_out4), .in1(or_2_out), .in2(decoder_1_out5), .in3(decoder_1_out15), .in4(decoder_1_out14),
    .in5(and_1_out), .in6(or_1_out), .in7(decoder_1_out13), .out(OUT), .gs(O));  // open: en_in, en_out
endmodule
