// Logisim project Вариант 26.circ as structural Verilog: 1 circuit, main circuit main
module main (
  input  \Сlk ,
  input  U,
  output [1:0] O1,
  output O0
);

  wire d_ff_1_q, d_ff_1_qn, demultiplexer_1_out0, demultiplexer_1_out1, j_k_ff_1_q, j_k_ff_1_qn, not_1_out;

  Demultiplexer #(.enable("false")) demultiplexer_1 (
    .out0(demultiplexer_1_out0), .out1(demultiplexer_1_out1), .in(\Сlk ), .sel(U));
  J_K_Flip_Flop j_k_ff_1 (
    .J(\Сlk ), .K(U), .Q(j_k_ff_1_q), .Qn(j_k_ff_1_qn), .en(demultiplexer_1_out0));  // open: clk, preset, reset
  D_Flip_Flop d_ff_1 (
    .clk(\Сlk ), .D(\Сlk ), .Q(d_ff_1_q), .Qn(d_ff_1_qn), .en(demultiplexer_1_out1));  // open: preset, reset
  not not_1 (not_1_out, demultiplexer_1_out1);
  Priority_Encoder #(.select(2)) priority_encoder_1 (
    .in0(j_k_ff_1_qn), .in1(d_ff_1_qn), .in2(j_k_ff_1_q), .in3(d_ff_1_q), .out(O1), .gs(O0), .en_in(not_1_out));  // open: en_out
endmodule
