// Logisim project Вариант 27.circ as structural Verilog: 1 circuit, main circuit main
module main (
  input  CLK,
  input  IN,
  output [9:0] OUT
);

  wire t_ff_1_qn, t_ff_2_qn, t_ff_3_qn, t_ff_4_qn, t_ff_5_qn, t_ff_6_qn, t_ff_7_qn, t_ff_8_qn, t_ff_9_qn;

  T_Flip_Flop t_ff_1 (.clk(CLK), .T(IN), .Q(OUT[0]), .Qn(t_ff_1_qn));  // open: preset, reset, en
  T_Flip_Flop t_ff_2 (.clk(t_ff_1_qn), .T(IN), .Q(OUT[1]), .Qn(t_ff_2_qn));  // open: preset, reset, en
  T_Flip_Flop t_ff_3 (.clk(t_ff_2_qn), .T(IN), .Q(OUT[2]), .Qn(t_ff_3_qn));  // open: preset, reset, en
  T_Flip_Flop t_ff_4 (.clk(t_ff_3_qn), .T(IN), .Q(OUT[3]), .Qn(t_ff_4_qn));  // open: preset, reset, en
  T_Flip_Flop t_ff_5 (.clk(t_ff_4_qn), .T(IN), .Q(OUT[4]), .Qn(t_ff_5_qn));  // open: preset, reset, en
  T_Flip_Flop t_ff_6 (.clk(t_ff_5_qn), .T(IN), .Q(OUT[5]), .Qn(t_ff_6_qn));  // open: preset, reset, en
  T_Flip_Flop t_ff_7 (.clk(t_ff_6_qn), .T(IN), .Qn(t_ff_7_qn));  // open: Q, preset, reset, en
  T_Flip_Flop t_ff_8 (.clk(t_ff_7_qn), .T(IN), .Q(OUT[7]), .Qn(t_ff_8_qn));  // open: preset, reset, en
  T_Flip_Flop t_ff_9 (.clk(t_ff_8_qn), .T(IN), .Q(OUT[8]), .Qn(t_ff_9_qn));  // open: preset, reset, en
  T_Flip_Flop t_ff_10 (.clk(t_ff_9_qn), .T(IN), .Q(OUT[9]));  // open: Qn, preset, reset, en
endmodule
