// Logisim project Вариант 28.circ as structural Verilog: 1 circuit, main circuit main
module main (
  input  S,
  input  CLK,
  input  R,
  input  in_4,
  input  S_2,
  input  En,
  input  R_2,
  output OUT
);

  wire decoder_1_out0, decoder_2_out0, decoder_2_out1, decoder_2_out6, decoder_2_out9, decoder_2_out10,
       decoder_2_out12, decoder_2_out13, multiplexer_2_out, s_r_ff_1_qn;
  wire [3:0] multiplexer_3_out;

  S_R_Flip_Flop s_r_ff_1 (
    .S(S), .clk(CLK), .R(R), .Q(multiplexer_3_out[1]), .Qn(s_r_ff_1_qn));  // open: preset, reset, en
  S_R_Flip_Flop s_r_ff_2 (.S(S_2), .clk(CLK), .R(R_2), .Q(multiplexer_3_out[2]));  // open: Qn, preset, reset, en
  Multiplexer #(.enable("false")) multiplexer_1 (
    .in0(multiplexer_3_out[1]), .in1(s_r_ff_1_qn), .out(multiplexer_3_out[3]), .sel(multiplexer_3_out[2]));
  Multiplexer #(.enable("false")) multiplexer_2 (
    .in0(multiplexer_3_out[1]), .in1(multiplexer_3_out[2]), .out(multiplexer_2_out),
    .sel(multiplexer_3_out[3]));
  Multiplexer #(.enable("false")) multiplexer_3 (
    .in0(multiplexer_3_out[2]), .in1(in_4), .out(multiplexer_3_out[0]), .sel(multiplexer_3_out[3]));
  Decoder #(.enable("false")) decoder_1 (.out0(decoder_1_out0), .sel(multiplexer_2_out));  // open: out1
  Decoder #(.select(4)) decoder_2 (
    .out0(decoder_2_out0), .out1(decoder_2_out1), .out6(decoder_2_out6), .out9(decoder_2_out9),
    .out10(decoder_2_out10), .out12(decoder_2_out12), .out13(decoder_2_out13), .sel(multiplexer_3_out),
    .en(En));  // open: out2, out3, out4, out5, out7, out8, out11, out14, out15
  or or_1 (OUT, decoder_1_out0, decoder_2_out0, decoder_2_out1, decoder_2_out6, decoder_2_out9, decoder_2_out10, decoder_2_out12, decoder_2_out13);
endmodule
